// Logisim project Sap1Evolution.circ as structural Verilog
module main (
);

  wire AddrReg_in, alu_1_r, ALUOpReg_in, ALUReg_in, ALUReg_out, ClearRam_out, clock_1_out, controller_1_p19,
       controller_1_p20, controller_1_p21, controller_1_p22, controller_1_p27, controller_1_p28, Halt,
       InstReg_in, InstReg_out, multiplexer_1_out, or_1_out, or_2_out, or_3_out, OutReg_in, PC_in, PC_inc,
       PC_out, Ram_in, Ram_out, RegA_in, RegA_out, RegB_in, RegB_out, Reset_out, ResetStepCounter,
       Video_Clear, Video_Draw;
  wire [2:0] StepCounter_q;
  wire [3:0] register_1_q, register_1_q_2;
  wire [5:0] ULAOPReg_q, videooperator_1_operator;
  wire [7:0] AddressReg_q, alu_1_s, InstructionReg_q, ProgramCounter_q, ram_1_data, RegA_q, RegB_q,
       subtractor_1_out, UlaReg_q, videooperator_1_we, videooperator_1_x_out, videooperator_1_y_out;
  wire [23:0] videooperator_1_color_out;

  Button Reset (.out(Reset_out));
  RAM #(.clearpin("true"), .databus("bidir"), .enables("line")) ram_1 (
    .addr(AddressReg_q), .we(Ram_in), .oe(Ram_out), .clk(or_1_out), .data(ram_1_data), .clr(ClearRam_out));
  Button ClearRam (.out(ClearRam_out));
  Hex_Digit_Display hex_digit_display_1 (.value(register_1_q_2));  // open: dp
  Hex_Digit_Display hex_digit_display_2 (.value(register_1_q));  // open: dp
  Register AddressReg (.D(ram_1_data), .en(AddrReg_in), .clk(or_1_out), .Q(AddressReg_q), .clr(Reset_out));
  Multiplexer multiplexer_1 (.in0(Halt), .in1(1'b0), .out(multiplexer_1_out), .sel(Reset_out));
  assign ram_1_data = PC_out ? ProgramCounter_q : 8'bz;  // Controlled_Buffer controlled_buffer_1
  Counter ProgramCounter (
    .load(PC_in), .D(ram_1_data), .count(PC_inc), .Q(ProgramCounter_q), .up(1'b1), .clk(or_1_out),
    .clr(Reset_out));  // open: carry
  Register register_1 (
    .D(ram_1_data), .en(OutReg_in), .clk(or_1_out), .Q({register_1_q_2, register_1_q}), .clr(Reset_out));
  Clock clock_1 (.out(clock_1_out));
  or or_1 (or_1_out, multiplexer_1_out, clock_1_out);
  assign ram_1_data = RegA_out ? RegA_q : 8'bz;  // Controlled_Buffer controlled_buffer_2
  assign ram_1_data = ALUReg_out ? UlaReg_q : 8'bz;  // Controlled_Buffer controlled_buffer_3
  assign ram_1_data = RegB_out ? RegB_q : 8'bz;  // Controlled_Buffer controlled_buffer_4
  assign ram_1_data = InstReg_out ? InstructionReg_q : 8'bz;  // Controlled_Buffer controlled_buffer_5
  // Probe on ram_1_data
  Register RegA (.D(ram_1_data), .en(RegA_in), .clk(or_1_out), .Q(RegA_q), .clr(Reset_out));
  Register RegB (.D(ram_1_data), .en(RegB_in), .clk(or_1_out), .Q(RegB_q), .clr(Reset_out));
  Register InstructionReg (.D(ram_1_data), .en(InstReg_in), .clk(or_1_out), .Q(InstructionReg_q), .clr(Reset_out));
  Counter #(.max('h7), .width(3)) StepCounter (
    .Q(StepCounter_q), .clk(or_1_out), .clr(or_2_out));  // open: load, D, count, carry, up
  or or_2 (or_2_out, Reset_out, ResetStepCounter);
  assign ram_1_data = ALUOpReg_in ? subtractor_1_out : 8'bz;  // Controlled_Buffer controlled_buffer_6
  Subtractor subtractor_1 (.a(InstructionReg_q), .b(8'h30), .out(subtractor_1_out));  // open: bin, bout
  Register #(.width(6)) ULAOPReg (
    .D(ram_1_data[5:0]), .en(ALUOpReg_in), .clk(or_1_out), .Q(ULAOPReg_q), .clr(Reset_out));
  // controller controller_1: pin names not known; wires that end beside it: InstructionReg_q, StepCounter_q, PC_out, PC_in, PC_inc, InstReg_out, InstReg_in, AddrReg_in, Ram_in, Ram_out, RegA_out, RegA_in, RegB_out, RegB_in, ALUReg_out, ALUReg_in, ALUOpReg_in, OutReg_in, controller_1_p19, controller_1_p20, controller_1_p21, controller_1_p22, Video_Draw, Video_Clear, ResetStepCounter, Halt, controller_1_p27, controller_1_p28
  assign ram_1_data = controller_1_p27 ? 8'h40 : 8'bz;  // Controlled_Buffer controlled_buffer_7
  ALU alu_1 (.Operator(ULAOPReg_q), .A(RegA_q), .B(RegB_q), .S(alu_1_s), .R(alu_1_r));
  // Probe on controller_1_p28
  Register UlaReg (.D(alu_1_s), .en(ALUReg_in), .clk(or_1_out), .Q(UlaReg_q), .clr(Reset_out));
  or or_3 (or_3_out, controller_1_p21, Reset_out);
  D_Flip_Flop Overflow (.D(alu_1_r), .reset(Reset_out));  // open: clk, Q, Qn, preset
  D_Flip_Flop Equality (.D(alu_1_r), .reset(Reset_out));  // open: clk, Q, Qn, preset
  D_Flip_Flop Result (.D(alu_1_r), .reset(Reset_out));  // open: clk, Q, Qn, preset
  VideoOperator videooperator_1 (
    .SET_WE(controller_1_p19), .Write(controller_1_p20), .WriteFromResult(controller_1_p22),
    .Reset(or_3_out), .Clock(or_1_out), .BusIn(ram_1_data), .Operator(videooperator_1_operator),
    .WE(videooperator_1_we), .X_out(videooperator_1_x_out), .Y_out(videooperator_1_y_out),
    .Color_out(videooperator_1_color_out));
  // RGB_Video #(.height(256), .scale(3), .width(256)) rgb_video_1: pin names not known; wires that end beside it: Video_Clear, or_1_out, Video_Draw, videooperator_1_x_out, videooperator_1_y_out, videooperator_1_color_out
  // Probe on videooperator_1_operator
  // Probe on videooperator_1_we
  // Probe on videooperator_1_x_out
  // Probe on videooperator_1_y_out
  // Probe on videooperator_1_color_out
endmodule

module Tests (
);

  wire alu_1_r, button_1_out, button_2_out, button_3_out, controller_1_addressreg_in,
       controller_1_equalityflag_out, controller_1_instructionreg_in, controller_1_instructionreg_out,
       controller_1_outreg_in, controller_1_overflowflag_out, controller_1_programcounter_in,
       controller_1_programcounter_increment, controller_1_programcounter_out, controller_1_ram_in,
       controller_1_ram_out, controller_1_rega_in, controller_1_rega_out, controller_1_regb_in,
       controller_1_regb_out, controller_1_resultflag_out, controller_1_ulaopreg_in, controller_1_ulareg_in,
       controller_1_ulareg_out, controller_1_video_draw, controller_1_video_in, controller_1_video_reset,
       controller_1_video_set_we, controller_1_video_write_from_result, dipswitch_1_sw1, dipswitch_1_sw2,
       dipswitch_1_sw3, keyboard_1_avail, t_ff_1_q, t_ff_1_qn, undriven, undriven_2;
  wire [2:0] keyboard_1_data_2, slider_2_out;
  wire [3:0] keyboard_1_data, register_1_q, register_2_q;
  wire [5:0] bit_extender_1_out, register_3_q;
  wire [7:0] alu_1_s, register_4_q, register_5_q, register_6_q, slider_1_out, slider_3_out;

  T_Flip_Flop t_ff_1 (.T(1'b1), .clk(keyboard_1_avail), .Q(t_ff_1_q), .Qn(t_ff_1_qn));  // open: reset, preset
  Keyboard keyboard_1 (
    .clk(keyboard_1_avail), .clr(button_1_out), .avail(keyboard_1_avail),
    .data({keyboard_1_data_2, keyboard_1_data}));  // open: re
  Button button_1 (.out(button_1_out));
  Register #(.width(4)) register_1 (
    .D(keyboard_1_data), .en(t_ff_1_q), .clk(keyboard_1_avail), .Q(register_1_q));  // open: clr
  Register #(.width(4)) register_2 (
    .D(keyboard_1_data), .en(t_ff_1_qn), .clk(keyboard_1_avail), .Q(register_2_q));  // open: clr
  // Probe on {register_2_q, register_1_q}
  // Probe on {register_2_q, register_1_q}
  Bit_Extender #(.out_width(6), .\type ("zero")) bit_extender_1 (
    .in({register_2_q, register_1_q}), .out(bit_extender_1_out));
  DipSwitch dipswitch_1 (
    .sw1(dipswitch_1_sw1), .sw2(dipswitch_1_sw2), .sw3(dipswitch_1_sw3));  // open: sw4, sw5, sw6, sw7, sw8
  Register #(.width(6)) register_3 (
    .D(bit_extender_1_out), .clk(dipswitch_1_sw1), .Q(register_3_q), .clr(undriven));  // open: en
  Register register_4 (
    .D({register_2_q, register_1_q}), .clk(dipswitch_1_sw2), .Q(register_4_q), .clr(undriven));  // open: en
  Register register_5 (
    .D({register_2_q, register_1_q}), .clk(dipswitch_1_sw3), .Q(register_5_q), .clr(undriven));  // open: en
  Button button_2 (.out(button_2_out));
  // Probe on register_4_q
  // Probe on register_5_q
  Slider slider_1 (.out(slider_1_out));
  Slider #(.width(3)) slider_2 (.out(slider_2_out));
  Slider slider_3 (.out(slider_3_out));
  // Probe on register_4_q
  // Probe on register_5_q
  // Probe on alu_1_s
  // Probe on alu_1_s
  ALU alu_1 (.Operator(register_3_q), .A(register_4_q), .B(register_5_q), .S(alu_1_s), .R(alu_1_r));
  // Probe on undriven_2
  // Probe on alu_1_r
  Register register_6 (.D(alu_1_s), .clk(button_3_out), .Q(register_6_q));  // open: en, clr
  Button button_3 (.out(button_3_out));
  // Probe on controller_1_programcounter_out
  controller controller_1 (
    .opCode(slider_1_out), .step(slider_2_out), .busIn(slider_3_out),
    .programCounter_out(controller_1_programcounter_out), .programCounter_in(controller_1_programcounter_in),
    .programCounter_increment(controller_1_programcounter_increment),
    .instructionReg_out(controller_1_instructionreg_out), .instructionReg_in(controller_1_instructionreg_in),
    .addressReg_in(controller_1_addressreg_in), .ram_in(controller_1_ram_in), .ram_out(controller_1_ram_out),
    .regA_out(controller_1_rega_out), .regA_in(controller_1_rega_in), .regB_out(controller_1_regb_out),
    .regB_in(controller_1_regb_in), .ulaReg_out(controller_1_ulareg_out), .ulaReg_in(controller_1_ulareg_in),
    .ulaOpReg_in(controller_1_ulaopreg_in), .outReg_in(controller_1_outreg_in),
    .overflowFlag_out(controller_1_overflowflag_out), .resultFlag_out(controller_1_resultflag_out),
    .equalityFlag_out(controller_1_equalityflag_out), .video_set_we(controller_1_video_set_we),
    .video_in(controller_1_video_in), .video_reset(controller_1_video_reset),
    .video_write_from_result(controller_1_video_write_from_result), .video_draw(controller_1_video_draw));  // open: video_clear_screen, resetStepCounter, halt, busOut_en, busOut
  // Probe on controller_1_programcounter_in
  // Probe on controller_1_programcounter_increment
  // Probe on controller_1_instructionreg_out
  // Probe on controller_1_instructionreg_in
  // Probe on controller_1_addressreg_in
  // Probe on controller_1_ram_in
  // Probe on controller_1_ram_out
  // Probe on controller_1_rega_out
  // Probe on controller_1_rega_in
  // Probe on controller_1_regb_out
  // Probe on controller_1_regb_in
  // Probe on controller_1_ulareg_out
  // Probe on controller_1_ulareg_in
  // Probe on controller_1_ulaopreg_in
  // Probe on controller_1_outreg_in
  // Probe on controller_1_overflowflag_out
  // Probe on controller_1_resultflag_out
  // Probe on controller_1_equalityflag_out
  // Probe on controller_1_video_set_we
  // Probe on controller_1_video_in
  // Probe on controller_1_video_reset
  // Probe on controller_1_video_write_from_result
  // Probe on controller_1_video_draw
  // Probe on alu_1_s
  // Probe on {register_6_q, alu_1_s}
endmodule

module ALU (
  input  [5:0] Operator,
  input  [7:0] A,
  input  [7:0] B,
  output [7:0] S,
  output R
);

  wire adder_2_cout, comparator_1_eq, comparator_1_gt, comparator_1_lt, comparator_2_eq, multiplexer_9_out,
       multiplexer_10_out, multiplexer_11_out, or_3_out, or_4_out, subtractor_2_bout;
  wire [7:0] adder_1_out, adder_2_out, and_1_out, bit_extender_1_out, bit_extender_2_out, bit_extender_3_out,
       bit_extender_4_out, bit_extender_5_out, divider_1_out, divider_1_rem, multiplexer_1_out,
       multiplexer_2_out, multiplexer_3_out, multiplexer_4_out, multiplexer_5_out, multiplexer_6_out,
       multiplexer_7_out, multiplier_1_cout, multiplier_1_out, negator_1_out, negator_2_out, not_1_out,
       not_2_out, not_3_out, not_4_out, not_5_out, or_1_out, or_2_out, shifter_1_out, shifter_2_out,
       subtractor_1_out, subtractor_2_out, xor_1_out;
  wire [8:0] random_1_out;

  Multiplexer #(.width(8)) multiplexer_1 (.in0(A), .in1(B), .out(multiplexer_1_out), .sel(Operator[0]));
  assign not_1_out = ~A;  // NOT_Gate not_1, 8 bits wide
  assign not_2_out = ~B;  // NOT_Gate not_2, 8 bits wide
  assign and_1_out = A & B;  // AND_Gate and_1, 8 bits wide
  assign or_1_out = A | B;  // OR_Gate or_1, 8 bits wide
  assign xor_1_out = A ^ B;  // XOR_Gate xor_1, 8 bits wide
  Shifter shifter_1 (.in(A), .\dist (B[2:0]), .out(shifter_1_out));
  Shifter #(.shift("lr")) shifter_2 (.in(A), .\dist (B[2:0]), .out(shifter_2_out));
  Comparator comparator_1 (.a(A), .b(B), .gt(comparator_1_gt), .eq(comparator_1_eq), .lt(comparator_1_lt));
  Multiplexer #(.width(8)) multiplexer_2 (.in0(A), .in1(B), .out(multiplexer_2_out), .sel(comparator_1_lt));
  Negator negator_1 (.in(A), .out(negator_1_out));
  Negator negator_2 (.in(B), .out(negator_2_out));
  Adder adder_1 (.a(multiplexer_1_out), .b(8'h1), .out(adder_1_out));  // open: cin, cout
  Subtractor subtractor_1 (.a(multiplexer_1_out), .b(8'h1), .out(subtractor_1_out));  // open: bin, bout
  Adder adder_2 (.a(A), .b(B), .out(adder_2_out), .cout(adder_2_cout));  // open: cin
  Subtractor subtractor_2 (.a(A), .b(B), .out(subtractor_2_out), .bout(subtractor_2_bout));  // open: bin
  Multiplier multiplier_1 (.a(A), .b(B), .out(multiplier_1_out), .cout(multiplier_1_cout));  // open: cin
  Divider divider_1 (.a(A), .b(B), .out(divider_1_out), .rem(divider_1_rem));  // open: upper
  assign or_2_out = not_1_out | B;  // OR_Gate or_2, 8 bits wide
  assign bit_extender_1_out = {{7{1'b0}}, comparator_1_eq};  // Bit_Extender bit_extender_1
  assign bit_extender_2_out = {{7{1'b0}}, comparator_1_gt};  // Bit_Extender bit_extender_2
  assign bit_extender_3_out = {{7{1'b0}}, or_3_out};  // Bit_Extender bit_extender_3
  or or_3 (or_3_out, comparator_1_gt, comparator_1_eq);
  assign bit_extender_4_out = {{7{1'b0}}, comparator_1_lt};  // Bit_Extender bit_extender_4
  assign bit_extender_5_out = {{7{1'b0}}, or_4_out};  // Bit_Extender bit_extender_5
  or or_4 (or_4_out, comparator_1_eq, comparator_1_lt);
  Multiplexer #(.width(8)) multiplexer_3 (.in0(B), .in1(A), .out(multiplexer_3_out), .sel(comparator_1_lt));
  Random #(.width(9)) random_1 (.next(comparator_2_eq), .clk(comparator_2_eq), .out(random_1_out));  // open: clr
  Comparator #(.width(6)) comparator_2 (.a(Operator), .b(6'b001111), .eq(comparator_2_eq));  // open: gt, lt
  assign not_3_out = ~and_1_out;  // NOT_Gate not_3, 8 bits wide
  assign not_4_out = ~or_1_out;  // NOT_Gate not_4, 8 bits wide
  assign not_5_out = ~xor_1_out;  // NOT_Gate not_5, 8 bits wide
  Multiplexer #(.select(4), .width(8)) multiplexer_4 (
    .in0(not_1_out), .in1(not_2_out), .in2(and_1_out), .in3(not_3_out), .in4(or_1_out), .in5(not_4_out),
    .in6(xor_1_out), .in7(not_5_out), .in8(or_2_out), .in9(shifter_1_out), .in10(shifter_2_out),
    .in11(bit_extender_1_out), .in12(bit_extender_2_out), .in13(bit_extender_3_out),
    .in14(bit_extender_4_out), .in15(bit_extender_5_out), .out(multiplexer_4_out), .sel(Operator[3:0]));
  Multiplexer #(.select(4), .width(8)) multiplexer_5 (
    .in0(multiplexer_2_out), .in1(multiplexer_3_out), .in15(random_1_out[7:0]), .out(multiplexer_5_out),
    .sel(Operator[3:0]));  // open: in2, in3, in4, in5, in6, in7, in8, in9, in10, in11, in12, in13, in14
  Multiplexer #(.select(4), .width(8)) multiplexer_6 (
    .in0(negator_1_out), .in1(negator_2_out), .in2(adder_1_out), .in3(adder_1_out), .in4(subtractor_1_out),
    .in5(subtractor_1_out), .in6(adder_2_out), .in7(subtractor_2_out), .in8(multiplier_1_out),
    .in9(multiplier_1_cout), .in10(divider_1_out), .in11(divider_1_rem), .out(multiplexer_6_out),
    .sel(Operator[3:0]));  // open: in12, in13, in14, in15
  Multiplexer #(.select(4), .width(8)) multiplexer_7 (
    .out(multiplexer_7_out), .sel(Operator[3:0]));  // open: in0, in1, in2, in3, in4, in5, in6, in7, in8, in9, in10, in11, in12, in13, in14, in15
  Multiplexer #(.select(2), .width(8)) multiplexer_8 (
    .in0(multiplexer_4_out), .in1(multiplexer_5_out), .in2(multiplexer_6_out), .in3(multiplexer_7_out),
    .out(S), .sel(Operator[5:4]));
  Multiplexer #(.select(4)) multiplexer_9 (
    .in15(random_1_out[8]), .out(multiplexer_9_out), .sel(Operator[3:0]));  // open: in0, in1, in2, in3, in4, in5, in6, in7, in8, in9, in10, in11, in12, in13, in14
  Multiplexer #(.select(4)) multiplexer_10 (
    .in2(adder_2_cout), .in3(subtractor_2_bout), .out(multiplexer_10_out), .sel(Operator[3:0]));  // open: in0, in1, in4, in5, in6, in7, in8, in9, in10, in11, in12, in13, in14, in15
  Multiplexer #(.select(4)) multiplexer_11 (
    .out(multiplexer_11_out), .sel(Operator[3:0]));  // open: in0, in1, in2, in3, in4, in5, in6, in7, in8, in9, in10, in11, in12, in13, in14, in15
  Multiplexer #(.select(2)) multiplexer_12 (
    .in0(multiplexer_4_out[0]), .in1(multiplexer_9_out), .in2(multiplexer_10_out), .in3(multiplexer_11_out),
    .out(R), .sel(Operator[5:4]));
endmodule

module SQRT (
  input  [7:0] in_1,
  input  [7:0] in_2,
  output [7:0] out_3,
  output out_4
);

  Multiplier multiplier_1 ();  // open: a, b, out, cin, cout
endmodule

module VideoOperator (
  input  SET_WE,
  input  Write,
  input  WriteFromResult,
  input  Reset,
  input  Clock,
  input  [7:0] BusIn,
  output [5:0] Operator,
  output [7:0] WE,
  output [7:0] X_out,
  output [7:0] Y_out,
  output [23:0] Color_out
);

  wire not_1_out;
  wire [7:0] alu_1_s, alu_2_s, alu_3_s, alu_4_s, alu_5_s, and_1_out, bit_extender_1_out, multiplexer_1_out,
       multiplexer_2_out, multiplexer_3_out, multiplexer_4_out, multiplexer_5_out, VideoOperand_q, Y_q;
  wire [7:6] Operator_Reg_q;

  Register WriteEnables (.D(BusIn), .en(SET_WE), .clk(Clock), .Q(WE), .clr(Reset));
  not not_1 (not_1_out, WriteFromResult);
  Multiplexer #(.width(8)) multiplexer_1 (.in0(alu_1_s), .in1(BusIn), .out(multiplexer_1_out), .sel(not_1_out));
  Multiplexer #(.width(8)) multiplexer_2 (.in0(alu_2_s), .in1(BusIn), .out(multiplexer_2_out), .sel(not_1_out));
  Multiplexer #(.width(8)) multiplexer_3 (.in0(alu_3_s), .in1(BusIn), .out(multiplexer_3_out), .sel(not_1_out));
  Multiplexer #(.width(8)) multiplexer_4 (.in0(alu_4_s), .in1(BusIn), .out(multiplexer_4_out), .sel(not_1_out));
  Multiplexer #(.width(8)) multiplexer_5 (.in0(alu_5_s), .in1(BusIn), .out(multiplexer_5_out), .sel(not_1_out));
  assign bit_extender_1_out = {{7{Write}}, Write};  // Bit_Extender bit_extender_1
  assign and_1_out = WE & bit_extender_1_out;  // AND_Gate and_1, 8 bits wide
  Register VideoOperand (.D(BusIn), .en(and_1_out[5]), .clk(Clock), .Q(VideoOperand_q), .clr(Reset));
  Register X (.D(multiplexer_1_out), .en(and_1_out[0]), .clk(Clock), .Q(X_out), .clr(Reset));
  Register Y (.D(multiplexer_2_out), .en(and_1_out[1]), .clk(Clock), .Q(Y_q), .clr(Reset));
  Register Operator_Reg (.D(BusIn), .en(and_1_out[6]), .clk(Clock), .Q({Operator_Reg_q, Operator}), .clr(Reset));
  Register R (.D(multiplexer_3_out), .en(and_1_out[2]), .clk(Clock), .Q(Color_out[7:0]), .clr(Reset));
  Register G (.D(multiplexer_4_out), .en(and_1_out[3]), .clk(Clock), .Q(Color_out[15:8]), .clr(Reset));
  Register B (.D(multiplexer_5_out), .en(and_1_out[4]), .clk(Clock), .Q(Color_out[23:16]), .clr(Reset));
  ALU alu_1 (.Operator(Operator), .A(X_out), .B(VideoOperand_q), .S(alu_1_s));  // open: R
  ALU alu_2 (.Operator(Operator), .A(Y_q), .B(VideoOperand_q), .S(alu_2_s));  // open: R
  ALU alu_3 (.Operator(Operator), .A(Color_out[7:0]), .B(VideoOperand_q), .S(alu_3_s));  // open: R
  ALU alu_4 (.Operator(Operator), .A(Color_out[15:8]), .B(VideoOperand_q), .S(alu_4_s));  // open: R
  ALU alu_5 (.Operator(Operator), .A(Color_out[23:16]), .B(VideoOperand_q), .S(alu_5_s));  // open: R
  Subtractor subtractor_1 (.a({8{1'b1}}), .b(Y_q), .out(Y_out));  // open: bin, bout

  // Notes on the sheet:
  //   Bitmask:
  //   0-op-O-B-G-R-Y-X
endmodule

// VHDL entity controller, as the project stores it:
LIBRARY ieee;
USE ieee.std_logic_1164.ALL;
USE ieee.numeric_std.ALL;

ENTITY controller IS
  PORT (
    -- Insert input ports below
    opCode        : IN  std_logic_vector(7 DOWNTO 0);
    step          : IN  std_logic_vector(2 DOWNTO 0);
    busIn       : IN  std_logic_vector(7 DOWNTO 0);
    -- Insert output ports below
    programCounter_out        : OUT std_logic;
    programCounter_in         : OUT std_logic;
    programCounter_increment  : OUT std_logic;
    instructionReg_out        : OUT std_logic;
    instructionReg_in         : OUT std_logic;
    addressReg_in             : OUT std_logic;
    ram_in                    : OUT std_logic;
    ram_out                   : OUT std_logic;
    regA_out                  : OUT std_logic;
    regA_in                   : OUT std_logic;
    regB_out                  : OUT std_logic;
    regB_in                   : OUT std_logic;
    ulaReg_out                : OUT std_logic;
    ulaReg_in                 : OUT std_logic;
    ulaOpReg_in               : OUT std_logic;
    outReg_in                 : OUT std_logic;
    overflowFlag_out          : OUT std_logic;
    resultFlag_out            : OUT std_logic;
    equalityFlag_out          : OUT std_logic; 
    video_set_we              : OUT std_logic;
    video_in                  : OUT std_logic;
    video_reset               : OUT std_logic;
    video_write_from_result   : OUT std_logic;
    video_draw                : OUT std_logic;
    video_clear_screen        : OUT std_logic;
    resetStepCounter          : OUT std_logic;
    halt                      : OUT std_logic;
    busOut_en                 : OUT std_logic;
    busOut     			: OUT  std_logic_vector(7 DOWNTO 0)
  );
END controller;

-- Complete your VHDL description below

ARCHITECTURE typeArchitecture OF controller IS
  SIGNAL step_int : INTEGER;
  SIGNAL opCode_int : INTEGER;
BEGIN
  step_int <= TO_INTEGER(UNSIGNED(step));
  opCode_int <= TO_INTEGER(UNSIGNED(opCode));
  PROCESS (step_int) BEGIN     
    instructionReg_out <= '0';
    instructionReg_in <= '0';  
    programCounter_out <= '0';
    programCounter_in <= '0';
    programCounter_increment <= '0';
    addressReg_in <= '0';
    ram_in <= '0';
    ram_out <= '0';
    regA_out <= '0';
    regA_in <= '0';
    regB_out <= '0';
    regB_in <= '0';
    ulaReg_out <= '0';
    ulaReg_in <= '0';
    ulaOpReg_in <= '0';
    outReg_in <= '0';
    overflowFlag_out <= '0';
    resultFlag_out <= '0';
    equalityFlag_out <= '0';
    video_set_we <= '0';
    video_in <= '0';
    video_reset <= '0';
    video_write_from_result <= '0';
    video_draw <= '0';
    video_clear_screen <= '0';
    resetStepCounter <= '0';
    halt <= '0';
    busOut_en <= '0';
    busOut <= "00000000";
    CASE step_int IS
		WHEN 0 => -- get address for next instruction
			programCounter_out <= '1';
			addressReg_in <= '1';            	   	    
			programCounter_increment <= '1';
		WHEN 1 => -- get instruction
			ram_out <= '1';                    	        
			instructionReg_in <= '1';
		WHEN 2 =>
		-- LOAD and SAVE OPERATORS
			CASE opCode_int IS
				WHEN 1 TO 4 | 16 TO 19 | 32 TO 34 | 113 TO 122 | 144 | 254 => -- get address part from the instruction.
				    programCounter_increment <= '1';
				    programCounter_out <= '1';
				    addressReg_in <= '1';
				WHEN 20 => 
				    ulaReg_out <= '1';
				    regA_in <= '1';                    	   
				WHEN 21 =>
				    ulaReg_out <= '1';
				    regB_in <= '1';
				WHEN 22 =>
				    equalityFlag_out <= '1';
				    regA_in <= '1';
				WHEN 23 =>
				    equalityFlag_out <= '1';
				    regB_in <= '1';
				WHEN 48 TO 111 =>
				    ulaOpReg_in <= '1';
				    -- Video Instructions
				WHEN 112 =>
				    video_draw <= '1';				
				WHEN 190 => -- define color clear later
				WHEN 191 => video_clear_screen <= '1';
				WHEN 255 => halt <= '1';             	
				WHEN OTHERS =>
				    resetStepCounter <= '1';
			 END CASE;
		WHEN 3 =>
			CASE opCode_int IS
				-- LOAD OPERATORS          		
				WHEN 16 TO 17 | 32 TO 34 | 254 => -- get address that contains the information.
				    ram_out <= '1';
				    addressReg_in <= '1';		                    	
				WHEN 1 => 
				    ram_out <= '1';
				    programCounter_in <= '1';                     		
				WHEN 18 =>
				    ram_out <= '1';
				    regA_in <= '1';     
				WHEN 19 =>
				    ram_out <= '1';
				    regB_in <= '1';     
				-- ULA Operators
				WHEN 48 TO 111 => ulaReg_in <= '1';
				-- Video from instruction
				WHEN 113 TO 117 =>
				    ram_out <= '1';				    
				    video_set_we <= '1';
				WHEN 144 =>
				    busOut_en <= '1';
				    busOut <= "01000000";
				    video_set_we <= '1';
				-- Skip empty last steps
				WHEN OTHERS => 
				    resetStepCounter <= '1';	        		
	     	END CASE;
		WHEN 4 =>
			CASE opCode_int IS
				-- LOAD and SAVE OPERATORS
				WHEN 16 =>
				    ram_out <= '1';
				    regA_in <= '1';
				WHEN 17 =>
				    ram_out <= '1';
				    regB_in <= '1';
				WHEN 32 =>
				    ram_in <= '1';
				    regA_out <= '1';
				WHEN 33 =>
				    ram_in <= '1';
				    regB_out <= '1';
				WHEN 34 =>
				    ram_in <= '1';
				    ulaReg_out <= '1';
				WHEN 82 | 84 => 
				    ulaReg_out <= '1';
				    regA_in <= '1';
				WHEN 83 | 85 => 
				    ulaReg_out <= '1';
				    regB_in <= '1';
				when 113 TO 114=>
				    programCounter_increment <= '1';
				    programCounter_out <= '1';
				    addressReg_in <= '1';
				when 115 =>
					regA_out <= '1';
					video_in <= '1';
				when 116 =>
					regB_out <= '1';
					video_in <= '1';
				when 117 =>
					ulaReg_out <= '1';
					video_in <= '1';			
				when 144 =>				
				     ram_out <= '1';
				     video_in <= '1';
				WHEN 254 => 
				    ram_out <= '1';
				    outReg_in <= '1';
				WHEN OTHERS =>  
				    resetStepCounter <= '1';
			END CASE;
		WHEN 5 =>
			CASE opCode_int IS
				-- LOAD and SAVE OPERATORbusOut_enS
				WHEN 113 =>
					ram_out <= '1';
				     addressReg_in <= '1';
				WHEN 114 =>
					ram_out <= '1';
				     video_in <= '1';
				WHEN 144 =>
				    programCounter_increment <= '1';
				    programCounter_out <= '1';
				    addressReg_in <= '1';	
				WHEN OTHERS =>  
				    resetStepCounter <= '1';
			END CASE;		
		WHEN 6 =>
			CASE opCode_int IS
				-- LOAD and SAVE OPERATORS
				WHEN 115 =>								
					ram_out <= '1';
				     video_in <= '1';
				WHEN 144 =>
				    ram_out <= '1';
				    video_set_we <= '1';
				WHEN OTHERS =>  
				    resetStepCounter <= '1';
			END CASE;				    
		WHEN 7 =>
			CASE opCode_int IS
				WHEN 144 =>
					video_write_from_result <= '1';
				    	video_in <= '1';
	     		WHEN OTHERS =>    		                    	
	         			resetStepCounter <= '1';
	 		END CASE;
		WHEN OTHERS =>                
		END CASE;
	END PROCESS;
END typeArchitecture;
